// Logisim project 16bitExtender.circ as structural Verilog: 1 circuit, main circuit 16bitExtender
// Extend
module _16bitExtender (
  input  [5:0] IMM,
  input  ExtendOp,
  output [15:0] IMM16
);

  wire [15:0] bit_extender_1_out, bit_extender_2_out;

  assign bit_extender_1_out = {{10{1'b0}}, IMM};  // Bit_Extender bit_extender_1
  assign bit_extender_2_out = {{10{IMM[5]}}, IMM};  // Bit_Extender bit_extender_2
  Multiplexer #(.width(16)) multiplexer_1 (
    .in0(bit_extender_1_out), .in1(bit_extender_2_out), .out(IMM16), .sel(ExtendOp));  // open: en
endmodule
