// Logisim project Arithmetic.circ as structural Verilog
// 1BitARTH
module _1_bit_Arithmetic_unit (
  input  carry_in,
  input  A,
  input  B,
  input  Binvert,
  output result,
  output carry_out
);

  wire multiplexer_1_out, not_1_out;

  not not_1 (not_1_out, B);
  Multiplexer multiplexer_1 (.in0(B), .in1(not_1_out), .out(multiplexer_1_out), .sel(Binvert));  // open: en
  Adder #(.width(1)) adder_1 (.a(A), .b(multiplexer_1_out), .out(result), .cin(carry_in), .cout(carry_out));
endmodule

// ARTH
module _16_bit_Arith (
  input  [15:0] A,
  input  [15:0] B,
  input  SUB,
  output [15:0] RESULT,
  output LessThan,
  output GreaterThan,
  output ZeroFlag,
  output OverFlow,
  output CARRYOUT
);

  wire n1_bit_arithmetic_unit_1_carry_out, n1_bit_arithmetic_unit_2_carry_out,
       n1_bit_arithmetic_unit_3_carry_out, n1_bit_arithmetic_unit_4_carry_out,
       n1_bit_arithmetic_unit_5_carry_out, n1_bit_arithmetic_unit_6_carry_out,
       n1_bit_arithmetic_unit_7_carry_out, n1_bit_arithmetic_unit_8_carry_out,
       n1_bit_arithmetic_unit_9_carry_out, n1_bit_arithmetic_unit_10_carry_out,
       n1_bit_arithmetic_unit_11_carry_out, n1_bit_arithmetic_unit_12_carry_out,
       n1_bit_arithmetic_unit_13_carry_out, n1_bit_arithmetic_unit_14_carry_out,
       n1_bit_arithmetic_unit_15_carry_out, not_1_out, not_2_out;

  _1_bit_Arithmetic_unit u_1_bit_arithmetic_unit_1 (
    .A(A[0]), .Binvert(SUB), .result(RESULT[0]), .carry_in(SUB),
    .carry_out(n1_bit_arithmetic_unit_1_carry_out), .B(B[0]));
  _1_bit_Arithmetic_unit u_1_bit_arithmetic_unit_2 (
    .A(A[1]), .Binvert(SUB), .result(RESULT[1]), .carry_in(n1_bit_arithmetic_unit_1_carry_out),
    .carry_out(n1_bit_arithmetic_unit_2_carry_out), .B(B[1]));
  _1_bit_Arithmetic_unit u_1_bit_arithmetic_unit_3 (
    .A(A[2]), .Binvert(SUB), .result(RESULT[2]), .carry_in(n1_bit_arithmetic_unit_2_carry_out),
    .carry_out(n1_bit_arithmetic_unit_3_carry_out), .B(B[2]));
  _1_bit_Arithmetic_unit u_1_bit_arithmetic_unit_4 (
    .A(A[3]), .Binvert(SUB), .result(RESULT[3]), .carry_in(n1_bit_arithmetic_unit_3_carry_out),
    .carry_out(n1_bit_arithmetic_unit_4_carry_out), .B(B[3]));
  _1_bit_Arithmetic_unit u_1_bit_arithmetic_unit_5 (
    .A(A[4]), .Binvert(SUB), .result(RESULT[4]), .carry_in(n1_bit_arithmetic_unit_4_carry_out),
    .carry_out(n1_bit_arithmetic_unit_5_carry_out), .B(B[4]));
  _1_bit_Arithmetic_unit u_1_bit_arithmetic_unit_6 (
    .A(A[5]), .Binvert(SUB), .result(RESULT[5]), .carry_in(n1_bit_arithmetic_unit_5_carry_out),
    .carry_out(n1_bit_arithmetic_unit_6_carry_out), .B(B[5]));
  _1_bit_Arithmetic_unit u_1_bit_arithmetic_unit_7 (
    .A(A[6]), .Binvert(SUB), .result(RESULT[6]), .carry_in(n1_bit_arithmetic_unit_6_carry_out),
    .carry_out(n1_bit_arithmetic_unit_7_carry_out), .B(B[6]));
  _1_bit_Arithmetic_unit u_1_bit_arithmetic_unit_8 (
    .A(A[7]), .Binvert(SUB), .result(RESULT[7]), .carry_in(n1_bit_arithmetic_unit_7_carry_out),
    .carry_out(n1_bit_arithmetic_unit_8_carry_out), .B(B[7]));
  _1_bit_Arithmetic_unit u_1_bit_arithmetic_unit_9 (
    .A(A[8]), .Binvert(SUB), .result(RESULT[8]), .carry_in(n1_bit_arithmetic_unit_8_carry_out),
    .carry_out(n1_bit_arithmetic_unit_9_carry_out), .B(B[8]));
  _1_bit_Arithmetic_unit u_1_bit_arithmetic_unit_10 (
    .A(A[9]), .Binvert(SUB), .result(RESULT[9]), .carry_in(n1_bit_arithmetic_unit_9_carry_out),
    .carry_out(n1_bit_arithmetic_unit_10_carry_out), .B(B[9]));
  _1_bit_Arithmetic_unit u_1_bit_arithmetic_unit_11 (
    .A(A[10]), .Binvert(SUB), .result(RESULT[10]), .carry_in(n1_bit_arithmetic_unit_10_carry_out),
    .carry_out(n1_bit_arithmetic_unit_11_carry_out), .B(B[10]));
  _1_bit_Arithmetic_unit u_1_bit_arithmetic_unit_12 (
    .A(A[11]), .Binvert(SUB), .result(RESULT[11]), .carry_in(n1_bit_arithmetic_unit_11_carry_out),
    .carry_out(n1_bit_arithmetic_unit_12_carry_out), .B(B[11]));
  _1_bit_Arithmetic_unit u_1_bit_arithmetic_unit_13 (
    .A(A[12]), .Binvert(SUB), .result(RESULT[12]), .carry_in(n1_bit_arithmetic_unit_12_carry_out),
    .carry_out(n1_bit_arithmetic_unit_13_carry_out), .B(B[12]));
  _1_bit_Arithmetic_unit u_1_bit_arithmetic_unit_14 (
    .A(A[13]), .Binvert(SUB), .result(RESULT[13]), .carry_in(n1_bit_arithmetic_unit_13_carry_out),
    .carry_out(n1_bit_arithmetic_unit_14_carry_out), .B(B[13]));
  _1_bit_Arithmetic_unit u_1_bit_arithmetic_unit_15 (
    .A(A[14]), .Binvert(SUB), .result(RESULT[14]), .carry_in(n1_bit_arithmetic_unit_14_carry_out),
    .carry_out(n1_bit_arithmetic_unit_15_carry_out), .B(B[14]));
  _1_bit_Arithmetic_unit u_1_bit_arithmetic_unit_16 (
    .A(A[15]), .Binvert(SUB), .result(LessThan), .carry_in(n1_bit_arithmetic_unit_15_carry_out),
    .carry_out(CARRYOUT), .B(B[15]));
  not not_1 (not_1_out, LessThan);
  not not_2 (not_2_out, ZeroFlag);
  nor nor_1 (ZeroFlag, RESULT[0], RESULT[1], RESULT[2], RESULT[3], RESULT[4], RESULT[5], RESULT[6], RESULT[7], RESULT[8], RESULT[9], RESULT[10], RESULT[11], RESULT[12], RESULT[13], RESULT[14], LessThan);
  xor xor_1 (OverFlow, n1_bit_arithmetic_unit_15_carry_out, CARRYOUT);
  and and_1 (GreaterThan, not_1_out, not_2_out);

  assign RESULT[15] = LessThan;

  // Other names for the same wires on the sheet: BI = SUB
endmodule

// AND
module _16bit_AND (
  input  [15:0] A,
  input  [15:0] B,
  output [15:0] out_3
);

  and and_1 (out_3[0], A[0], B[0]);
  and and_2 (out_3[1], A[1], B[1]);
  and and_3 (out_3[2], A[2], B[2]);
  and and_4 (out_3[3], A[3], B[3]);
  and and_5 (out_3[4], A[4], B[4]);
  and and_6 (out_3[5], A[5], B[5]);
  and and_7 (out_3[6], A[6], B[6]);
  and and_8 (out_3[7], A[7], B[7]);
  and and_9 (out_3[8], A[8], B[8]);
  and and_10 (out_3[9], A[9], B[9]);
  and and_11 (out_3[10], A[10], B[10]);
  and and_12 (out_3[11], A[11], B[11]);
  and and_13 (out_3[12], A[12], B[12]);
  and and_14 (out_3[13], A[13], B[13]);
  and and_15 (out_3[14], A[14], B[14]);
  and and_16 (out_3[15], A[15], B[15]);
endmodule

// OR
module _16bit_OR (
  input  [15:0] A,
  input  [15:0] B,
  output [15:0] out_3
);

  or or_1 (out_3[0], A[0], B[0]);
  or or_2 (out_3[1], A[1], B[1]);
  or or_3 (out_3[2], A[2], B[2]);
  or or_4 (out_3[3], A[3], B[3]);
  or or_5 (out_3[4], A[4], B[4]);
  or or_6 (out_3[5], A[5], B[5]);
  or or_7 (out_3[6], A[6], B[6]);
  or or_8 (out_3[7], A[7], B[7]);
  or or_9 (out_3[8], A[8], B[8]);
  or or_10 (out_3[9], A[9], B[9]);
  or or_11 (out_3[10], A[10], B[10]);
  or or_12 (out_3[11], A[11], B[11]);
  or or_13 (out_3[12], A[12], B[12]);
  or or_14 (out_3[13], A[13], B[13]);
  or or_15 (out_3[14], A[14], B[14]);
  or or_16 (out_3[15], A[15], B[15]);
endmodule

// XOR
module _16bit_XOR (
  input  [15:0] A,
  input  [15:0] B,
  output [15:0] out_3
);

  xor xor_1 (out_3[0], A[0], B[0]);
  xor xor_2 (out_3[1], A[1], B[1]);
  xor xor_3 (out_3[2], A[2], B[2]);
  xor xor_4 (out_3[3], A[3], B[3]);
  xor xor_5 (out_3[4], A[4], B[4]);
  xor xor_6 (out_3[5], A[5], B[5]);
  xor xor_7 (out_3[6], A[6], B[6]);
  xor xor_8 (out_3[7], A[7], B[7]);
  xor xor_9 (out_3[8], A[8], B[8]);
  xor xor_10 (out_3[9], A[9], B[9]);
  xor xor_11 (out_3[10], A[10], B[10]);
  xor xor_12 (out_3[11], A[11], B[11]);
  xor xor_13 (out_3[12], A[12], B[12]);
  xor xor_14 (out_3[13], A[13], B[13]);
  xor xor_15 (out_3[14], A[14], B[14]);
  xor xor_16 (out_3[15], A[15], B[15]);
endmodule

module _16bit_LogicUnit (
  input  [15:0] A,
  input  [15:0] B,
  input  [1:0] OP,
  output [15:0] out_4
);

  wire [15:0] n16bit_and_1_out_3, n16bit_or_1_out_3, n16bit_xor_1_out_3, not_1_out;

  _16bit_AND u_16bit_and_1 (.A(A), .B(B), .out_3(n16bit_and_1_out_3));
  _16bit_OR u_16bit_or_1 (.A(A), .B(B), .out_3(n16bit_or_1_out_3));
  _16bit_XOR u_16bit_xor_1 (.A(A), .B(B), .out_3(n16bit_xor_1_out_3));
  assign not_1_out = ~n16bit_or_1_out_3;  // NOT_Gate not_1, 16 bits wide
  Multiplexer #(.select(2), .width(16)) multiplexer_1 (
    .in0(n16bit_and_1_out_3), .in1(n16bit_or_1_out_3), .in2(not_1_out), .in3(n16bit_xor_1_out_3),
    .out(out_4), .sel(OP));  // open: en
endmodule

module _16bit_ShiftUnit (
  input  [15:0] A,
  input  [15:0] B,
  input  [1:0] OP,
  output [15:0] out_4
);

  wire [15:0] shifter_1_out, shifter_2_out, shifter_3_out, shifter_4_out;

  Shifter #(.width(16)) shifter_1 (.in(A), .\dist (B[3:0]), .out(shifter_1_out));
  Shifter #(.width(16), .shift("lr")) shifter_2 (.in(A), .\dist (B[3:0]), .out(shifter_2_out));
  Shifter #(.width(16), .shift("ar")) shifter_3 (.in(A), .\dist (B[3:0]), .out(shifter_3_out));
  Shifter #(.width(16), .shift("rl")) shifter_4 (.in(A), .\dist (B[3:0]), .out(shifter_4_out));
  Multiplexer #(.select(2), .width(16)) multiplexer_1 (
    .in0(shifter_1_out), .in1(shifter_2_out), .in2(shifter_3_out), .in3(shifter_4_out), .out(out_4), .sel(OP));  // open: en
endmodule
