// Logisim project CPU.circ as structural Verilog: 4 circuits, main circuit main
module main (
);

  wire AluSrc, AluSrc_Ex, and_2_out, and_3_out, BRAANCH, BRANCH, BZ, CarryOut, CLK, constReg, constReg_Ex,
       Equal, Equal_Ex, ExtendOp, greaterThan, J, J_Ex, JALR_Ex, JR_ID, JUMP, kill1, kill2, lessThan, LUI,
       LUI_Ex, MemRd, MemRd_Ex, MemRd_MEM, MemToReg, MemToReg_Ex, MemToReg_MEM, MemWr, MemWr_Ex, MemWr_MEM,
       not_1_out, not_2_out, or_1_out, overFlow, RegDst, RegDst_Ex, RegWr, RegWr_Ex, RegWr_MEM, RegWr_WB,
       SetLess, SetLess_Ex, stall, TrueB, Unsigned, Unsigned_Ex, ZeroFlag;
  wire [1:0] ALU_OP, ALU_OP_Ex, forward_A, forward_B, Op_type, Op_type_Ex;
  wire [2:0] constRegV, DstReg, DstReg_Ex, DstReg_MEM, DstReg_WB, FUNCTION, multiplexer_6_out, Rd, Rs, Rt,
       Rt_Ex;
  wire [3:0] OP_code, OP_code_Ex;
  wire [15:0] A_Ex, A_ID, B_Ex, B_ID, B_MEM, Br_PC, Br_PC_Ex, ImmEX16, ImmEX16_Ex, Instruction,
       Instruction_ID, instructiondecoder_1_j_pc, J_PC, LessThanResult, LUIMM, LUIMM_Ex, memOutput,
       multiplexer_1_out, multiplexer_2_out, multiplexer_3_out, multiplexer_4_out, multiplexer_11_out, PC,
       PC_1, PC_1_Ex, PC_1_ID, PC_1_WB, PC_ID, registerfile_1_data_1, registerfile_1_data_2, Result,
       Result_MEM, WD1, WD2, WD3, WrData_Ex, WrData_Ex_MEM, WrData_MEM, WrData_WB;

  Clock u_CLK (.out(CLK));
  Multiplexer #(.width(16)) multiplexer_1 (.in0(PC_1), .in1(PC), .out(multiplexer_1_out), .sel(stall));  // open: en
  Adder #(.width(16)) adder_1 (.a(PC), .b(16'h1), .out(PC_1));  // open: cin, cout
  Multiplexer #(.width(16)) multiplexer_2 (
    .in0(multiplexer_1_out), .in1(J_PC), .out(multiplexer_2_out), .sel(JUMP));  // open: en
  Multiplexer #(.width(16)) multiplexer_3 (
    .in0(multiplexer_2_out), .in1(Br_PC_Ex), .out(multiplexer_3_out), .sel(BRAANCH));  // open: en
  PC u_pc_1 (.newPc(multiplexer_3_out), .CLK(CLK), .PC(PC));  // open: Reset
  ROM #(.addrWidth(16), .dataWidth(16)) rom_1 (.addr(PC), .data(Instruction));  // open: sel
  Multiplexer #(.width(16)) multiplexer_4 (
    .in0(Instruction), .in1({16{1'b0}}), .out(multiplexer_4_out), .sel(kill1));  // open: en
  IF_ID if_id_1 (
    .PC(PC), .INSTRUCTION(multiplexer_4_out), .out_5(PC_ID), .out_6(Instruction_ID), .CLK(CLK),
    .enable(not_1_out));
  not not_1 (not_1_out, stall);
  InstructionDecoder instructiondecoder_1 (
    .INSTRUCTION(Instruction_ID), .OP_CODE(OP_code), .Rs(Rs), .Rt(Rt), .Rd(Rd), .FUNCTION(FUNCTION),
    .ImmEX16(ImmEX16), .LUIMM(LUIMM), .J_PC(instructiondecoder_1_j_pc), .Br_PC(Br_PC), .PC(PC_ID));
  Adder #(.width(16)) adder_2 (.a(PC_ID), .b(16'h1), .out(PC_1_ID));  // open: cin, cout
  Multiplexer #(.width(16)) multiplexer_5 (
    .in0(instructiondecoder_1_j_pc), .in1(A_ID), .out(J_PC), .sel(JR_ID));  // open: en
  Multiplexer #(.width(3)) multiplexer_6 (.in0(Rt), .in1(Rd), .out(multiplexer_6_out), .sel(RegDst));  // open: en
  Multiplexer #(.width(3)) multiplexer_7 (
    .in0(multiplexer_6_out), .in1(constRegV), .out(DstReg), .sel(constReg));  // open: en
  not not_2 (not_2_out, RegWr);
  and and_1 (JR_ID, RegDst, not_2_out, J);
  RegisterFile registerfile_1 (
    .Read_Register_1(Rs), .Read_Register_2(Rt), .Write_Register(DstReg_WB), .Write_Data(WrData_WB),
    .Data_1(registerfile_1_data_1), .Data_2(registerfile_1_data_2), .regWrite(RegWr_WB), .Clock(CLK));
  Multiplexer #(.select(2), .width(16)) multiplexer_8 (
    .in0(registerfile_1_data_1), .in1(WrData_Ex), .in2(WrData_MEM), .in3(WrData_WB), .out(A_ID),
    .sel(forward_A));  // open: en
  Multiplexer #(.select(2), .width(16)) multiplexer_9 (
    .in0(registerfile_1_data_2), .in1(WrData_Ex), .in2(WrData_MEM), .in3(WrData_WB), .out(B_ID),
    .sel(forward_B));  // open: en
  PC_Control pc_control_1 (.TrueB(TrueB), .J(J), .Branch(BRAANCH), .Kill_2(kill2), .Jump(JUMP), .Kill_1(kill1));
  Control_unit control_unit_1 (
    .OPcode(OP_code), .Function(FUNCTION), .RegDst(RegDst), .RegWr(RegWr), .ExtendOp(ExtendOp),
    .AluSrc(AluSrc), .MemRd(MemRd), .MemWr(MemWr), .MemToReg(MemToReg), .BRANCH(BRANCH), .JUMP(J),
    .SeltLess(SetLess), .Equal(Equal), .Unsigned(Unsigned), .ALU_OP(ALU_OP), .OP_TYPE(Op_type), .BZ(BZ),
    .LUI(LUI), .CONSTREG(constReg));
  Multiplexer #(.width(3)) multiplexer_10 (.in0(3'b111), .in1(3'b001), .out(constRegV), .sel(and_2_out));  // open: en
  and and_2 (and_2_out, LUI, constReg);
  forwarding_unit forwarding_unit_1 (
    .DstReg_Ex(DstReg_Ex), .DstReg_MEM(DstReg_MEM), .A_ID(Rs), .B_ID(Rt), .MEMREAD_EX(MemRd_Ex),
    .stall(stall), .DstReg_WB(DstReg_WB), .forward_B(forward_B), .forward_A(forward_A));
  ID_EX id_ex_1 (
    .BTA(Br_PC), .IMMEDIATE(ImmEX16), .BUS_A(A_ID), .BUS_B(B_ID), .DesReg(DstReg), .BTA_2(Br_PC_Ex),
    .IMMEDIATE_2(ImmEX16_Ex), .BUS_A_2(A_Ex), .BUS_B_2(B_Ex), .DesReg_2(DstReg_Ex), .CLK(CLK),
    .OpCode(OP_code), .OpCode_2(OP_code_Ex), .Rt(Rt), .ALU_OP(ALU_OP), .Rt_2(Rt_Ex), .ALU_OP_2(ALU_OP_Ex),
    .OP_Type(Op_type), .OP_Type_2(Op_type_Ex), .ALU_SRC(AluSrc), .Unsigned(Unsigned), .Equal(Equal),
    .ALU_SRC_2(AluSrc_Ex), .Unsigned_2(Unsigned_Ex), .Equal_2(Equal_Ex), .MemWrite(MemWr),
    .MemWrite_2(MemWr_Ex), .MemRead(MemRd), .MemRead_2(MemRd_Ex), .RegWrite(RegWr), .RegWrite_2(RegWr_Ex),
    .J(J), .J_2(J_Ex), .MemToReg(MemToReg), .MemToReg_2(MemToReg_Ex), .LUI(LUI), .LUI_2(LUI_Ex),
    .ConstReg(constReg), .ConstReg_2(constReg_Ex), .Set_Less(SetLess), .Set_Less_2(SetLess_Ex),
    .PC___1(PC_1_ID), .PC___1_2(PC_1_Ex), .LUIMM(LUIMM), .LUIMM_2(LUIMM_Ex), .RegDst(RegDst),
    .RegDst_2(RegDst_Ex), .Stall(or_1_out));
  or or_1 (or_1_out, stall, kill2);
  Multiplexer #(.width(16)) multiplexer_11 (
    .in0(B_Ex), .in1(ImmEX16_Ex), .out(multiplexer_11_out), .sel(AluSrc_Ex));  // open: en
  Multiplexer #(.width(16)) multiplexer_12 (.in0(WD1), .in1(WD2), .out(WD3), .sel(constReg_Ex));  // open: en
  Multiplexer #(.width(16)) multiplexer_13 (.in0(WD3), .in1(PC_1_WB), .out(WrData_Ex), .sel(JALR_Ex));  // open: en
  ALU alu_1 (
    .A(A_Ex), .B(multiplexer_11_out), .lessThan(lessThan), .greaterThan(greaterThan), .overFlow(overFlow),
    .zeroFlag(ZeroFlag), .carryOut(CarryOut), .Result(Result), .OP(ALU_OP_Ex), .op_type(Op_type_Ex));
  comp_contUnit comp_contunit_1 (
    .Unsigned(Unsigned_Ex), .Equal(Equal_Ex), .Lessthan(lessThan), .zeroFlag(ZeroFlag), .carryOut(CarryOut),
    .LessThanResult(LessThanResult));
  Branch_control_unit branch_control_unit_1 (
    .opCode(OP_code_Ex), .RT(Rt_Ex), .ZeroFlag(ZeroFlag), .LessThan(lessThan), .GreaterThan(greaterThan),
    .Branch(TrueB));
  Multiplexer #(.width(16)) multiplexer_14 (
    .in0(Result), .in1(LessThanResult), .out(WD1), .sel(SetLess_Ex));  // open: en
  Multiplexer #(.width(16)) multiplexer_15 (.in0(PC_1_Ex), .in1(LUIMM_Ex), .out(WD2), .sel(and_3_out));  // open: en
  and and_3 (and_3_out, LUI_Ex, constReg_Ex);
  and and_4 (JALR_Ex, RegDst_Ex, RegWr_Ex, J_Ex);
  EX_MEM ex_mem_1 (
    .Result(Result), .B(B_Ex), .DesReg(DstReg_Ex), .MemWrite(MemWr_Ex), .MemRead(MemRd_Ex),
    .RegWrite(RegWr_Ex), .MemToReg(MemToReg_Ex), .Result_2(Result_MEM), .B_2(B_MEM), .DesReg_2(DstReg_MEM),
    .MemWrite_2(MemWr_MEM), .MemRead_2(MemRd_MEM), .RegWrite_2(RegWr_MEM), .MemToReg_2(MemToReg_MEM),
    .CLK(CLK), .WrData(WrData_Ex), .WrData_2(WrData_Ex_MEM));  // open: PC___1, LUIMM, LessThan_Result, J, LUI, ConstReg, Set_Less, PC___1_2, LUIMM_2, LessThan_Result_2, J_2, LUI_2, ConstReg_2, Set_Less_2, RegDst, RegDst_2
  RAM #(.addrWidth(16), .dataWidth(16), .bus("separate")) ram_1 (
    .addr(Result_MEM), .din(B_MEM), .data(memOutput), .str(MemWr_MEM), .clk(CLK), .ld(MemRd_MEM));  // open: sel, clr
  Multiplexer #(.width(16)) multiplexer_16 (
    .in0(WrData_Ex_MEM), .in1(memOutput), .out(WrData_MEM), .sel(MemToReg_MEM));  // open: en
  MEM_WB mem_wb_1 (
    .WrData(WrData_MEM), .DesReg(DstReg_MEM), .RegWrite(RegWr_MEM), .WrData_2(WrData_WB),
    .DesReg_2(DstReg_WB), .RegWrite_2(RegWr_WB), .in_4(CLK));

  // Notes on the sheet:
  //   PC
  //   INSTRCION MEMORY
  //   contents of rom_1 (hex, n*v repeats v):
  //   a384 8354 35b 2040 2081 20c2 890a 1921 1520 14f2 4c02 1290 403b 3100 b012 55c 1b68 403f 4e9 2040
  //   2285 22c6 4e0 3100 1e06
  //   CONTROL UNIT
  //   ALU
  //   RAM
endmodule

module RegisterFile (
  input  [2:0] Read_Register_1,
  input  [2:0] Read_Register_2,
  input  [2:0] Write_Register,
  input  regWrite,
  input  Clock,
  input  [15:0] Write_Data,
  output [15:0] Data_1,
  output [15:0] Data_2
);

  wire and_1_out, and_2_out, and_3_out, and_4_out, and_5_out, and_6_out, and_7_out, and_8_out,
       decoder_1_out0, decoder_1_out1, decoder_1_out2, decoder_1_out3, decoder_1_out4, decoder_1_out5,
       decoder_1_out6, decoder_1_out7;
  wire [15:0] register_1_q, register_2_q, register_3_q, register_4_q, register_5_q, register_6_q,
       register_7_q, register_8_q;

  Decoder #(.select(3)) decoder_1 (
    .out0(decoder_1_out0), .out1(decoder_1_out1), .out2(decoder_1_out2), .out3(decoder_1_out3),
    .out4(decoder_1_out4), .out5(decoder_1_out5), .out6(decoder_1_out6), .out7(decoder_1_out7),
    .sel(Write_Register));  // open: en
  and and_1 (and_1_out, decoder_1_out0, 1'b0, regWrite);
  and and_2 (and_2_out, decoder_1_out1, regWrite);
  and and_3 (and_3_out, decoder_1_out2, regWrite);
  and and_4 (and_4_out, decoder_1_out3, regWrite);
  and and_5 (and_5_out, decoder_1_out4, regWrite);
  and and_6 (and_6_out, decoder_1_out5, regWrite);
  and and_7 (and_7_out, decoder_1_out6, regWrite);
  and and_8 (and_8_out, decoder_1_out7, regWrite);
  Register #(.width(16)) register_1 (.D(Write_Data), .en(and_1_out), .Q(register_1_q), .clk(Clock));  // open: clr
  Register #(.width(16)) register_2 (.D(Write_Data), .en(and_2_out), .Q(register_2_q), .clk(Clock));  // open: clr
  Register #(.width(16)) register_3 (.D(Write_Data), .en(and_3_out), .Q(register_3_q), .clk(Clock));  // open: clr
  Register #(.width(16)) register_4 (.D(Write_Data), .en(and_4_out), .Q(register_4_q), .clk(Clock));  // open: clr
  Register #(.width(16)) register_5 (.D(Write_Data), .en(and_5_out), .Q(register_5_q), .clk(Clock));  // open: clr
  Register #(.width(16)) register_6 (.D(Write_Data), .en(and_6_out), .Q(register_6_q), .clk(Clock));  // open: clr
  Register #(.width(16)) register_7 (.D(Write_Data), .en(and_7_out), .Q(register_7_q), .clk(Clock));  // open: clr
  Register #(.width(16)) register_8 (.D(Write_Data), .en(and_8_out), .Q(register_8_q), .clk(Clock));  // open: clr
  Multiplexer #(.select(3), .width(16)) multiplexer_1 (
    .in0(register_1_q), .in1(register_2_q), .in2(register_3_q), .in3(register_4_q), .in4(register_5_q),
    .in5(register_6_q), .in6(register_7_q), .in7(register_8_q), .out(Data_2), .sel(Read_Register_2));  // open: en
  Multiplexer #(.select(3), .width(16)) multiplexer_2 (
    .in0(register_1_q), .in1(register_2_q), .in2(register_3_q), .in3(register_4_q), .in4(register_5_q),
    .in5(register_6_q), .in6(register_7_q), .in7(register_8_q), .out(Data_1), .sel(Read_Register_1));  // open: en
endmodule

// LessThan_contUnit
module comp_contUnit (
  input  Unsigned,
  input  Equal,
  input  Lessthan,
  input  zeroFlag,
  input  carryOut,
  output [15:0] LessThanResult
);

  wire multiplexer_1_out, multiplexer_2_out, multiplexer_3_out, not_1_out, not_2_out, or_1_out, or_2_out;

  not not_1 (not_1_out, carryOut);
  or or_1 (or_1_out, Lessthan, zeroFlag);
  not not_2 (not_2_out, carryOut);
  or or_2 (or_2_out, not_1_out, zeroFlag);
  Multiplexer multiplexer_1 (.in0(Lessthan), .in1(or_1_out), .out(multiplexer_1_out), .sel(Equal));  // open: en
  Multiplexer multiplexer_2 (.in0(not_2_out), .in1(or_2_out), .out(multiplexer_2_out), .sel(Equal));  // open: en
  Multiplexer multiplexer_3 (
    .in0(multiplexer_1_out), .in1(multiplexer_2_out), .out(multiplexer_3_out), .sel(Unsigned));  // open: en
  assign LessThanResult = {{15{1'b0}}, multiplexer_3_out};  // Bit_Extender bit_extender_1
endmodule

// INSTRUCTION DECODER
module InstructionDecoder (
  input  [15:0] INSTRUCTION,
  input  [15:0] PC,
  output [2:0] Rs,
  output [2:0] Rt,
  output [2:0] Rd,
  output [3:0] OP_CODE,
  output [2:0] FUNCTION,
  output [15:0] ImmEX16,
  output [15:0] J_PC,
  output [15:0] LUIMM,
  output [15:0] Br_PC
);

  Shifter #(.width(16)) shifter_1 (.in(INSTRUCTION), .\dist (4'b0100), .out(LUIMM));
  assign ImmEX16 = {{10{INSTRUCTION[5]}}, INSTRUCTION[5:0]};  // Bit_Extender bit_extender_1
  Adder #(.width(16)) adder_1 (.a(PC), .b(ImmEX16), .out(Br_PC), .cin(1'b1));  // open: cout

  assign FUNCTION = INSTRUCTION[2:0];
  assign J_PC = {PC[15:12], INSTRUCTION[11:0]};
  assign OP_CODE = INSTRUCTION[15:12];
  assign Rd = INSTRUCTION[5:3];
  assign Rs = INSTRUCTION[11:9];
  assign Rt = INSTRUCTION[8:6];

  // Other names for the same wires on the sheet: last4[3:0] = PC[15:12]
endmodule
