// Logisim project Control_Unit_Main.circ as structural Verilog: 1 circuit, main circuit Control_unit
// Cont_unit
module Control_unit (
  input  [3:0] OPcode,
  input  [2:0] Function,
  output RegDst,
  output RegWr,
  output ExtendOp,
  output AluSrc,
  output MemRd,
  output MemWr,
  output MemToReg,
  output BRANCH,
  output BZ,
  output JUMP,
  output SeltLess,
  output Equal,
  output Unsigned,
  output LUI,
  output CONSTREG,
  output [1:0] ALU_OP,
  output [1:0] OP_TYPE
);

  wire ADD, ADDI, ADDING, AND, ANDI, ANDING, BEQ, BGT, BGTZ_BGEZ, BLT, BLTZ_BLEZ, BNE, decoder_2_out0,
       decoder_2_out1, decoder_2_out2, decoder_2_out3, decoder_2_out4, decoder_2_out5, decoder_2_out6,
       decoder_2_out7, decoder_3_out0, decoder_3_out1, decoder_3_out2, decoder_3_out3, decoder_3_out4,
       decoder_3_out5, decoder_3_out6, decoder_3_out7, J, JAL, JALR, JR, NOR, OR, or_14_out, or_15_out,
       or_16_out, or_17_out, or_18_out, or_19_out, or_20_out, ORI, ORING, ROL, Rtype1, Rtype2, SLL, SLT,
       SLTE, SLTEU, SLTU, SRA, SRL, SUB, SUBTRACTING, XOR;

  Decoder #(.select(4)) decoder_1 (
    .out0(Rtype1), .out1(Rtype2), .out2(MemRd), .out3(MemWr), .out4(BEQ), .out5(BNE), .out6(ANDI),
    .out7(ORI), .out8(ADDI), .out9(J), .out10(LUI), .out11(JAL), .out12(BLTZ_BLEZ), .out13(BLT),
    .out14(BGTZ_BGEZ), .out15(BGT), .sel(OPcode));  // open: en
  Decoder #(.select(3)) decoder_2 (
    .out0(decoder_2_out0), .out1(decoder_2_out1), .out2(decoder_2_out2), .out3(decoder_2_out3),
    .out4(decoder_2_out4), .out5(decoder_2_out5), .out6(decoder_2_out6), .out7(decoder_2_out7), .sel(Function));  // open: en
  Decoder #(.select(3)) decoder_3 (
    .out0(decoder_3_out0), .out1(decoder_3_out1), .out2(decoder_3_out2), .out3(decoder_3_out3),
    .out4(decoder_3_out4), .out5(decoder_3_out5), .out6(decoder_3_out6), .out7(decoder_3_out7), .sel(Function));  // open: en
  and and_1 (AND, decoder_2_out0, Rtype1);
  and and_2 (OR, decoder_2_out1, Rtype1);
  and and_3 (NOR, decoder_2_out2, Rtype1);
  and and_4 (XOR, decoder_2_out3, Rtype1);
  and and_5 (SLL, decoder_2_out4, Rtype1);
  and and_6 (SRL, decoder_2_out5, Rtype1);
  and and_7 (SRA, decoder_2_out6, Rtype1);
  and and_8 (ROL, decoder_2_out7, Rtype1);
  and and_9 (ADD, decoder_3_out0, Rtype2);
  and and_10 (SUB, decoder_3_out1, Rtype2);
  and and_11 (SLT, decoder_3_out2, Rtype2);
  and and_12 (SLTU, decoder_3_out3, Rtype2);
  and and_13 (SLTE, decoder_3_out4, Rtype2);
  and and_14 (SLTEU, decoder_3_out5, Rtype2);
  and and_15 (JR, decoder_3_out6, Rtype2);
  and and_16 (JALR, decoder_3_out7, Rtype2);
  or or_1 (RegDst, Rtype1, Rtype2);
  nor nor_1 (ExtendOp, ANDI, ORI);
  or or_2 (AluSrc, MemRd, MemWr, ANDI, ORI, ADDI);
  or or_3 (JUMP, JAL, J, JR, JALR);
  or or_4 (RegWr, Rtype1, ADD, SUB, SLT, SLTU, SLTE, SLTEU, JALR, MemRd, ANDI, ORI, ADDI, LUI, JAL);
  or or_5 (BRANCH, BEQ, BNE, BLTZ_BLEZ, BLT, BGTZ_BGEZ, BGT);
  or or_6 (SeltLess, SLT, SLTU, SLTE, SLTEU);
  or or_7 (Equal, SLTE, SLTEU);
  or or_8 (Unsigned, SLTU, SLTEU);
  or or_9 (BZ, BLTZ_BLEZ, BGTZ_BGEZ);
  or or_10 (ANDING, AND, ANDI);
  or or_11 (ORING, OR, ORI);
  or or_12 (ADDING, MemRd, MemWr, ADDI, ADD);
  or or_13 (SUBTRACTING, BRANCH, SeltLess, SUB);
  or or_14 (or_14_out, ADDING, ANDING, SLL);
  or or_15 (or_15_out, SUBTRACTING, ORING, SRL);
  or or_16 (or_16_out, NOR, SRA);
  or or_17 (or_17_out, XOR, ROL);
  or or_18 (or_18_out, ADDING, SUBTRACTING);
  or or_19 (or_19_out, ANDING, ORING, NOR, XOR);
  or or_20 (or_20_out, SLL, SRL, SRA, ROL);
  or or_21 (CONSTREG, LUI, JAL);
  Priority_Encoder #(.select(2)) priority_encoder_1 (
    .in0(or_14_out), .in1(or_15_out), .in2(or_16_out), .in3(or_17_out), .out(ALU_OP));  // open: gs, en_out, en_in
  Priority_Encoder #(.select(2)) priority_encoder_2 (
    .in0(or_18_out), .in1(or_19_out), .in2(or_20_out), .out(OP_TYPE));  // open: in3, gs, en_out, en_in

  assign MemToReg = MemRd;

  // Other names for the same wires on the sheet: BRANCH_WITH_ZERO = BZ; BRANCHING = BRANCH; ExetndOp = ExtendOp;
  //   FUNC[2:0] = Function; LW = MemRd; SETLESS = SeltLess; SW = MemWr
endmodule
