// Logisim project ExtMerge.circ as structural Verilog: 1 circuit, main circuit ext_merge
module ext_merge (
  input  [13:0] IMM,
  input  [1:0] last2,
  output [15:0] out_3
);

  Shifter #(.width(14)) shifter_1 (.in(IMM), .\dist (4'b0010), .out(out_3[13:0]));

  assign out_3[15:14] = last2;
endmodule
