// Logisim project PC CONTROL.circ as structural Verilog: 1 circuit, main circuit PC Control
module PC_Control (
  input  TrueB,
  input  J,
  output Branch,
  output Kill_2,
  output Jump,
  output Kill_1
);

  wire not_1_out;

  not not_1 (not_1_out, TrueB);
  and and_1 (Jump, not_1_out, J);
  or or_1 (Kill_1, Jump, TrueB);

  assign Branch = TrueB;
  assign Kill_2 = TrueB;
endmodule
