// Logisim project Registers Pipeline.circ as structural Verilog: 4 circuits, main circuit IF/ID
module IF_ID (
  input  [15:0] PC,
  input  [15:0] INSTRUCTION,
  input  CLK,
  input  enable,
  output [15:0] out_5,
  output [15:0] out_6
);

  Register #(.width(16)) u_PC (.D(PC), .en(enable), .Q(out_5), .clk(CLK));  // open: clr
  Register #(.width(16)) u_Instruction (.D(INSTRUCTION), .en(enable), .Q(out_6), .clk(CLK));  // open: clr
endmodule

module ID_EX (
  input  [15:0] BTA,
  input  [15:0] IMMEDIATE,
  input  [15:0] BUS_A,
  input  [15:0] BUS_B,
  input  [2:0] DesReg,
  input  [3:0] OpCode,
  input  [2:0] Rt,
  input  [1:0] ALU_OP,
  input  [1:0] OP_Type,
  input  ALU_SRC,
  input  Unsigned,
  input  Equal,
  input  MemWrite,
  input  MemRead,
  input  RegWrite,
  input  J,
  input  MemToReg,
  input  LUI,
  input  ConstReg,
  input  Set_Less,
  input  [15:0] PC___1,
  input  [15:0] LUIMM,
  input  RegDst,
  input  CLK,
  input  Stall,
  output [15:0] BTA_2,
  output [15:0] IMMEDIATE_2,
  output [15:0] BUS_A_2,
  output [15:0] BUS_B_2,
  output [2:0] DesReg_2,
  output [3:0] OpCode_2,
  output [2:0] Rt_2,
  output [1:0] ALU_OP_2,
  output [1:0] OP_Type_2,
  output ALU_SRC_2,
  output Unsigned_2,
  output Equal_2,
  output MemWrite_2,
  output MemRead_2,
  output RegWrite_2,
  output J_2,
  output MemToReg_2,
  output LUI_2,
  output ConstReg_2,
  output Set_Less_2,
  output [15:0] PC___1_2,
  output [15:0] LUIMM_2,
  output RegDst_2
);

  wire multiplexer_6_out, multiplexer_7_out, multiplexer_8_out, multiplexer_9_out, multiplexer_12_out,
       multiplexer_17_out, multiplexer_18_out, multiplexer_19_out, multiplexer_20_out, multiplexer_21_out,
       multiplexer_22_out, multiplexer_23_out;
  wire [1:0] multiplexer_15_out, multiplexer_16_out;
  wire [2:0] multiplexer_5_out, multiplexer_14_out;
  wire [3:0] multiplexer_13_out;
  wire [15:0] multiplexer_1_out, multiplexer_2_out, multiplexer_3_out, multiplexer_4_out, multiplexer_10_out,
       multiplexer_11_out;

  Multiplexer #(.width(16)) multiplexer_1 (
    .in0(BTA), .in1({16{1'b0}}), .out(multiplexer_1_out), .sel(Stall));  // open: en
  Multiplexer #(.width(16)) multiplexer_2 (
    .in0(IMMEDIATE), .in1({16{1'b0}}), .out(multiplexer_2_out), .sel(Stall));  // open: en
  Multiplexer #(.width(16)) multiplexer_3 (
    .in0(BUS_A), .in1({16{1'b0}}), .out(multiplexer_3_out), .sel(Stall));  // open: en
  Multiplexer #(.width(16)) multiplexer_4 (
    .in0(BUS_B), .in1({16{1'b0}}), .out(multiplexer_4_out), .sel(Stall));  // open: en
  Multiplexer #(.width(3)) multiplexer_5 (
    .in0(DesReg), .in1(3'b000), .out(multiplexer_5_out), .sel(Stall));  // open: en
  Multiplexer multiplexer_6 (.in0(Unsigned), .in1(1'b0), .out(multiplexer_6_out), .sel(Stall));  // open: en
  Multiplexer multiplexer_7 (.in0(RegWrite), .in1(1'b0), .out(multiplexer_7_out), .sel(Stall));  // open: en
  Multiplexer multiplexer_8 (.in0(J), .in1(1'b0), .out(multiplexer_8_out), .sel(Stall));  // open: en
  Multiplexer multiplexer_9 (.in0(LUI), .in1(1'b0), .out(multiplexer_9_out), .sel(Stall));  // open: en
  Multiplexer #(.width(16)) multiplexer_10 (
    .in0(PC___1), .in1({16{1'b0}}), .out(multiplexer_10_out), .sel(Stall));  // open: en
  Multiplexer #(.width(16)) multiplexer_11 (
    .in0(LUIMM), .in1({16{1'b0}}), .out(multiplexer_11_out), .sel(Stall));  // open: en
  Multiplexer multiplexer_12 (.in0(RegDst), .in1(1'b0), .out(multiplexer_12_out), .sel(Stall));  // open: en
  Multiplexer #(.width(4)) multiplexer_13 (
    .in0(OpCode), .in1(4'b0000), .out(multiplexer_13_out), .sel(Stall));  // open: en
  Multiplexer #(.width(3)) multiplexer_14 (.in0(Rt), .in1(3'b000), .out(multiplexer_14_out), .sel(Stall));  // open: en
  Multiplexer #(.width(2)) multiplexer_15 (
    .in0(ALU_OP), .in1(2'b00), .out(multiplexer_15_out), .sel(Stall));  // open: en
  Multiplexer #(.width(2)) multiplexer_16 (
    .in0(OP_Type), .in1(2'b00), .out(multiplexer_16_out), .sel(Stall));  // open: en
  Multiplexer multiplexer_17 (.in0(ALU_SRC), .in1(1'b0), .out(multiplexer_17_out), .sel(Stall));  // open: en
  Multiplexer multiplexer_18 (.in0(Equal), .in1(1'b0), .out(multiplexer_18_out), .sel(Stall));  // open: en
  Multiplexer multiplexer_19 (.in0(MemWrite), .in1(1'b0), .out(multiplexer_19_out), .sel(Stall));  // open: en
  Multiplexer multiplexer_20 (.in0(MemRead), .in1(1'b0), .out(multiplexer_20_out), .sel(Stall));  // open: en
  Multiplexer multiplexer_21 (.in0(MemToReg), .in1(1'b0), .out(multiplexer_21_out), .sel(Stall));  // open: en
  Multiplexer multiplexer_22 (.in0(ConstReg), .in1(1'b0), .out(multiplexer_22_out), .sel(Stall));  // open: en
  Multiplexer multiplexer_23 (.in0(Set_Less), .in1(1'b0), .out(multiplexer_23_out), .sel(Stall));  // open: en
  Register #(.width(16)) u_BTA (.D(multiplexer_1_out), .Q(BTA_2), .clk(CLK));  // open: en, clr
  Register #(.width(16)) u_Immediate (.D(multiplexer_2_out), .Q(IMMEDIATE_2), .clk(CLK));  // open: en, clr
  Register #(.width(16)) u_BUS_A (.D(multiplexer_3_out), .Q(BUS_A_2), .clk(CLK));  // open: en, clr
  Register #(.width(16)) u_BUS_B (.D(multiplexer_4_out), .Q(BUS_B_2), .clk(CLK));  // open: en, clr
  Register #(.width(3)) u_DesReg (.D(multiplexer_5_out), .Q(DesReg_2), .clk(CLK));  // open: en, clr
  Register #(.width(4)) u_OpCode (.D(multiplexer_13_out), .Q(OpCode_2), .clk(CLK));  // open: en, clr
  Register #(.width(3)) u_Rt (.D(multiplexer_14_out), .Q(Rt_2), .clk(CLK));  // open: en, clr
  Register #(.width(2)) u_ALU_OP (.D(multiplexer_15_out), .Q(ALU_OP_2), .clk(CLK));  // open: en, clr
  Register #(.width(2)) u_OP_Type (.D(multiplexer_16_out), .Q(OP_Type_2), .clk(CLK));  // open: en, clr
  Register #(.width(1)) u_ALU_SRC (.D(multiplexer_17_out), .Q(ALU_SRC_2), .clk(CLK));  // open: en, clr
  Register #(.width(1)) u_Unsigned (.D(multiplexer_6_out), .Q(Unsigned_2), .clk(CLK));  // open: en, clr
  Register #(.width(1)) u_Equal (.D(multiplexer_18_out), .Q(Equal_2), .clk(CLK));  // open: en, clr
  Register #(.width(1)) u_MemWrite (.D(multiplexer_19_out), .Q(MemWrite_2), .clk(CLK));  // open: en, clr
  Register #(.width(1)) u_MemRead (.D(multiplexer_20_out), .Q(MemRead_2), .clk(CLK));  // open: en, clr
  Register #(.width(1)) u_RegWrite (.D(multiplexer_7_out), .Q(RegWrite_2), .clk(CLK));  // open: en, clr
  Register #(.width(1)) u_J (.D(multiplexer_8_out), .Q(J_2), .clk(CLK));  // open: en, clr
  Register #(.width(1)) u_MemToReg (.D(multiplexer_21_out), .Q(MemToReg_2), .clk(CLK));  // open: en, clr
  Register #(.width(1)) u_LUI (.D(multiplexer_9_out), .Q(LUI_2), .clk(CLK));  // open: en, clr
  Register #(.width(1)) u_ConstReg (.D(multiplexer_22_out), .Q(ConstReg_2), .clk(CLK));  // open: en, clr
  Register #(.width(1)) u_Set_Less (.D(multiplexer_23_out), .Q(Set_Less_2), .clk(CLK));  // open: en, clr
  Register #(.width(16)) u_PC___1 (.D(multiplexer_10_out), .Q(PC___1_2), .clk(CLK));  // open: en, clr
  Register #(.width(16)) u_LUIMM (.D(multiplexer_11_out), .Q(LUIMM_2), .clk(CLK));  // open: en, clr
  Register #(.width(1)) u_RegDst (.D(multiplexer_12_out), .Q(RegDst_2), .clk(CLK));  // open: en, clr
endmodule

module EX_MEM (
  input  [15:0] WrData,
  input  [15:0] Result,
  input  [15:0] B,
  input  [2:0] DesReg,
  input  MemWrite,
  input  MemRead,
  input  [15:0] PC___1,
  input  [15:0] LUIMM,
  input  [15:0] LessThan_Result,
  input  RegWrite,
  input  J,
  input  MemToReg,
  input  LUI,
  input  ConstReg,
  input  Set_Less,
  input  RegDst,
  input  CLK,
  output [15:0] WrData_2,
  output [15:0] Result_2,
  output [15:0] B_2,
  output [2:0] DesReg_2,
  output MemWrite_2,
  output MemRead_2,
  output [15:0] PC___1_2,
  output [15:0] LUIMM_2,
  output [15:0] LessThan_Result_2,
  output RegWrite_2,
  output J_2,
  output MemToReg_2,
  output LUI_2,
  output ConstReg_2,
  output Set_Less_2,
  output RegDst_2
);

  Register #(.width(16)) u_WrData (.D(WrData), .Q(WrData_2), .clk(CLK));  // open: en, clr
  Register #(.width(16)) u_Result (.D(Result), .Q(Result_2), .clk(CLK));  // open: en, clr
  Register #(.width(16)) u_B (.D(B), .Q(B_2), .clk(CLK));  // open: en, clr
  Register #(.width(3)) u_DesReg (.D(DesReg), .Q(DesReg_2), .clk(CLK));  // open: en, clr
  Register #(.width(1)) u_MemWrite (.D(MemWrite), .Q(MemWrite_2), .clk(CLK));  // open: en, clr
  Register #(.width(1)) u_MemRead (.D(MemRead), .Q(MemRead_2), .clk(CLK));  // open: en, clr
  Register #(.width(16)) u_PC___1 (.D(PC___1), .Q(PC___1_2), .clk(CLK));  // open: en, clr
  Register #(.width(16)) u_LUIMM (.D(LUIMM), .Q(LUIMM_2), .clk(CLK));  // open: en, clr
  Register #(.width(16)) u_LessThan_Result (.D(LessThan_Result), .Q(LessThan_Result_2), .clk(CLK));  // open: en, clr
  Register #(.width(1)) u_RegWrite (.D(RegWrite), .Q(RegWrite_2), .clk(CLK));  // open: en, clr
  Register #(.width(1)) u_J (.D(J), .Q(J_2), .clk(CLK));  // open: en, clr
  Register #(.width(1)) u_MemToReg (.D(MemToReg), .Q(MemToReg_2), .clk(CLK));  // open: en, clr
  Register #(.width(1)) u_LUI (.D(LUI), .Q(LUI_2), .clk(CLK));  // open: en, clr
  Register #(.width(1)) u_ConstReg (.D(ConstReg), .Q(ConstReg_2), .clk(CLK));  // open: en, clr
  Register #(.width(1)) u_Set_Less (.D(Set_Less), .Q(Set_Less_2), .clk(CLK));  // open: en, clr
  Register #(.width(1)) u_RegDst (.D(RegDst), .Q(RegDst_2), .clk(CLK));  // open: en, clr
endmodule

module MEM_WB (
  input  [15:0] WrData,
  input  [2:0] DesReg,
  input  RegWrite,
  input  in_4,
  output [15:0] WrData_2,
  output [2:0] DesReg_2,
  output RegWrite_2
);

  Register #(.width(16)) u_WrData (.D(WrData), .Q(WrData_2), .clk(in_4));  // open: en, clr
  Register #(.width(3)) u_DesReg (.D(DesReg), .Q(DesReg_2), .clk(in_4));  // open: en, clr
  Register #(.width(1)) u_RegWrite (.D(RegWrite), .Q(RegWrite_2), .clk(in_4));  // open: en, clr
endmodule
