// Logisim project Registers Pipeline_.circ as structural Verilog: 4 circuits, main circuit IF/ID
module IF_ID (
  input  [15:0] PC,
  input  [15:0] INSTRUCTION,
  input  in_3,
  output [15:0] out_4,
  output [15:0] out_5
);

  Register #(.width(16)) u_PC (.D(PC), .Q(out_4), .clk(in_3));  // open: en, clr
  Register #(.width(16)) u_Instruction (.D(INSTRUCTION), .Q(out_5), .clk(in_3));  // open: en, clr
endmodule

module ID_EX (
  input  [15:0] BTA,
  input  [15:0] IMMEDIATE,
  input  [15:0] BUS_A,
  input  [15:0] BUS_B,
  input  [2:0] DesReg,
  input  [3:0] OpCode,
  input  [2:0] Rt,
  input  [1:0] ALU_OP,
  input  [1:0] OP_Type,
  input  ALU_SRC,
  input  Unsigned,
  input  Equal,
  input  MemWrite,
  input  MemRead,
  input  RegWrite,
  input  J,
  input  MemToReg,
  input  LUI,
  input  ConstReg,
  input  Set_Less,
  input  [15:0] PC___1,
  input  [15:0] LUIMM,
  input  RegDst,
  input  CLK,
  input  Stall,
  output [15:0] BTA_2,
  output [15:0] IMMEDIATE_2,
  output [15:0] BUS_A_2,
  output [15:0] BUS_B_2,
  output [2:0] DesReg_2,
  output [3:0] OpCode_2,
  output [2:0] Rt_2,
  output [1:0] ALU_OP_2,
  output [1:0] OP_Type_2,
  output ALU_SRC_2,
  output Unsigned_2,
  output Equal_2,
  output MemWrite_2,
  output MemRead_2,
  output RegWrite_2,
  output J_2,
  output MemToReg_2,
  output LUI_2,
  output ConstReg_2,
  output Set_Less_2,
  output [15:0] PC___1_2,
  output [15:0] LUIMM_2,
  output RegDst_2
);

  wire ALU_SRC_q, ConstReg_q, Equal_q, J_q, LUI_q, MemRead_q, MemToReg_q, MemWrite_q, RegDst_q, RegWrite_q,
       Set_Less_q, Unsigned_q;
  wire [1:0] ALU_OP_q, OP_Type_q;
  wire [2:0] DesReg_q, Rt_q;
  wire [3:0] OpCode_q;
  wire [15:0] BTA_q, BUS_A_q, BUS_B_q, Immediate_q, LUIMM_q, PC___1_q;

  Register #(.width(16)) u_BTA (.D(BTA), .Q(BTA_q), .clk(CLK));  // open: en, clr
  Register #(.width(16)) u_Immediate (.D(IMMEDIATE), .Q(Immediate_q), .clk(CLK));  // open: en, clr
  Register #(.width(16)) u_BUS_A (.D(BUS_A), .Q(BUS_A_q), .clk(CLK));  // open: en, clr
  Register #(.width(16)) u_BUS_B (.D(BUS_B), .Q(BUS_B_q), .clk(CLK));  // open: en, clr
  Register #(.width(3)) u_DesReg (.D(DesReg), .Q(DesReg_q), .clk(CLK));  // open: en, clr
  Register #(.width(4)) u_OpCode (.D(OpCode), .Q(OpCode_q), .clk(CLK));  // open: en, clr
  Register #(.width(3)) u_Rt (.D(Rt), .Q(Rt_q), .clk(CLK));  // open: en, clr
  Register #(.width(2)) u_ALU_OP (.D(ALU_OP), .Q(ALU_OP_q), .clk(CLK));  // open: en, clr
  Register #(.width(2)) u_OP_Type (.D(OP_Type), .Q(OP_Type_q), .clk(CLK));  // open: en, clr
  Register #(.width(1)) u_ALU_SRC (.D(ALU_SRC), .Q(ALU_SRC_q), .clk(CLK));  // open: en, clr
  Register #(.width(1)) u_Unsigned (.D(Unsigned), .Q(Unsigned_q), .clk(CLK));  // open: en, clr
  Register #(.width(1)) u_Equal (.D(Equal), .Q(Equal_q), .clk(CLK));  // open: en, clr
  Register #(.width(1)) u_MemWrite (.D(MemWrite), .Q(MemWrite_q), .clk(CLK));  // open: en, clr
  Register #(.width(1)) u_MemRead (.D(MemRead), .Q(MemRead_q), .clk(CLK));  // open: en, clr
  Register #(.width(1)) u_RegWrite (.D(RegWrite), .Q(RegWrite_q), .clk(CLK));  // open: en, clr
  Register #(.width(1)) u_J (.D(J), .Q(J_q), .clk(CLK));  // open: en, clr
  Register #(.width(1)) u_MemToReg (.D(MemToReg), .Q(MemToReg_q), .clk(CLK));  // open: en, clr
  Register #(.width(1)) u_LUI (.D(LUI), .Q(LUI_q), .clk(CLK));  // open: en, clr
  Register #(.width(1)) u_ConstReg (.D(ConstReg), .Q(ConstReg_q), .clk(CLK));  // open: en, clr
  Register #(.width(1)) u_Set_Less (.D(Set_Less), .Q(Set_Less_q), .clk(CLK));  // open: en, clr
  Register #(.width(16)) u_PC___1 (.D(PC___1), .Q(PC___1_q), .clk(CLK));  // open: en, clr
  Register #(.width(16)) u_LUIMM (.D(LUIMM), .Q(LUIMM_q), .clk(CLK));  // open: en, clr
  Register #(.width(1)) u_RegDst (.D(RegDst), .Q(RegDst_q), .clk(CLK));  // open: en, clr
  Multiplexer #(.width(16)) multiplexer_1 (.in0(BTA_q), .in1({16{1'b0}}), .out(BTA_2), .sel(Stall));  // open: en
  Multiplexer #(.width(16)) multiplexer_2 (
    .in0(Immediate_q), .in1({16{1'b0}}), .out(IMMEDIATE_2), .sel(Stall));  // open: en
  Multiplexer #(.width(16)) multiplexer_3 (.in0(BUS_A_q), .in1({16{1'b0}}), .out(BUS_A_2), .sel(Stall));  // open: en
  Multiplexer #(.width(16)) multiplexer_4 (.in0(BUS_B_q), .in1({16{1'b0}}), .out(BUS_B_2), .sel(Stall));  // open: en
  Multiplexer #(.width(3)) multiplexer_5 (.in0(DesReg_q), .in1(3'b000), .out(DesReg_2), .sel(Stall));  // open: en
  Multiplexer #(.width(4)) multiplexer_6 (.in0(OpCode_q), .in1(4'b0000), .out(OpCode_2), .sel(Stall));  // open: en
  Multiplexer #(.width(3)) multiplexer_7 (.in0(Rt_q), .in1(3'b000), .out(Rt_2), .sel(Stall));  // open: en
  Multiplexer #(.width(2)) multiplexer_8 (.in0(ALU_OP_q), .in1(2'b00), .out(ALU_OP_2), .sel(Stall));  // open: en
  Multiplexer #(.width(2)) multiplexer_9 (.in0(OP_Type_q), .in1(2'b00), .out(OP_Type_2), .sel(Stall));  // open: en
  Multiplexer multiplexer_10 (.in0(ALU_SRC_q), .in1(1'b0), .out(ALU_SRC_2), .sel(Stall));  // open: en
  Multiplexer multiplexer_11 (.in0(Unsigned_q), .in1(1'b0), .out(Unsigned_2), .sel(Stall));  // open: en
  Multiplexer multiplexer_12 (.in0(Equal_q), .in1(1'b0), .out(Equal_2), .sel(Stall));  // open: en
  Multiplexer multiplexer_13 (.in0(MemWrite_q), .in1(1'b0), .out(MemWrite_2), .sel(Stall));  // open: en
  Multiplexer multiplexer_14 (.in0(MemRead_q), .in1(1'b0), .out(MemRead_2), .sel(Stall));  // open: en
  Multiplexer multiplexer_15 (.in0(RegWrite_q), .in1(1'b0), .out(RegWrite_2), .sel(Stall));  // open: en
  Multiplexer multiplexer_16 (.in0(J_q), .in1(1'b0), .out(J_2), .sel(Stall));  // open: en
  Multiplexer multiplexer_17 (.in0(MemToReg_q), .in1(1'b0), .out(MemToReg_2), .sel(Stall));  // open: en
  Multiplexer multiplexer_18 (.in0(LUI_q), .in1(1'b0), .out(LUI_2), .sel(Stall));  // open: en
  Multiplexer multiplexer_19 (.in0(ConstReg_q), .in1(1'b0), .out(ConstReg_2), .sel(Stall));  // open: en
  Multiplexer multiplexer_20 (.in0(Set_Less_q), .in1(1'b0), .out(Set_Less_2), .sel(Stall));  // open: en
  Multiplexer #(.width(16)) multiplexer_21 (.in0(PC___1_q), .in1({16{1'b0}}), .out(PC___1_2), .sel(Stall));  // open: en
  Multiplexer #(.width(16)) multiplexer_22 (.in0(LUIMM_q), .in1({16{1'b0}}), .out(LUIMM_2), .sel(Stall));  // open: en
  Multiplexer multiplexer_23 (.in0(RegDst_q), .in1(1'b0), .out(RegDst_2), .sel(Stall));  // open: en
endmodule

module EX_MEM (
  input  [15:0] WrData,
  input  [15:0] Result,
  input  [15:0] B,
  input  [2:0] DesReg,
  input  MemWrite,
  input  MemRead,
  input  RegWrite,
  input  MemToReg,
  input  CLK,
  output [15:0] WrData_2,
  output [15:0] Result_2,
  output [15:0] B_2,
  output [2:0] DesReg_2,
  output MemWrite_2,
  output MemRead_2,
  output RegWrite_2,
  output MemToReg_2
);

  Register #(.width(16)) u_WrData (.D(WrData), .Q(WrData_2), .clk(CLK));  // open: en, clr
  Register #(.width(16)) u_Result (.D(Result), .Q(Result_2), .clk(CLK));  // open: en, clr
  Register #(.width(16)) u_B (.D(B), .Q(B_2), .clk(CLK));  // open: en, clr
  Register #(.width(3)) u_DesReg (.D(DesReg), .Q(DesReg_2), .clk(CLK));  // open: en, clr
  Register #(.width(1)) u_MemWrite (.D(MemWrite), .Q(MemWrite_2), .clk(CLK));  // open: en, clr
  Register #(.width(1)) u_MemRead (.D(MemRead), .Q(MemRead_2), .clk(CLK));  // open: en, clr
  Register #(.width(1)) u_RegWrite (.D(RegWrite), .Q(RegWrite_2), .clk(CLK));  // open: en, clr
  Register #(.width(1)) u_MemToReg (.D(MemToReg), .Q(MemToReg_2), .clk(CLK));  // open: en, clr
endmodule

module MEM_WB (
  input  [15:0] WrData,
  input  [2:0] DesReg,
  input  RegWrite,
  input  in_4,
  output [15:0] WrData_2,
  output [2:0] DesReg_2,
  output RegWrite_2
);

  Register #(.width(16)) u_WrData (.D(WrData), .Q(WrData_2), .clk(in_4));  // open: en, clr
  Register #(.width(3)) u_DesReg (.D(DesReg), .Q(DesReg_2), .clk(in_4));  // open: en, clr
  Register #(.width(1)) u_RegWrite (.D(RegWrite), .Q(RegWrite_2), .clk(in_4));  // open: en, clr
endmodule
