// Logisim project forwarding_unit.circ as structural Verilog: 1 circuit, main circuit forwarding_unit
module forwarding_unit (
  input  [2:0] DstReg_Ex,
  input  [2:0] DstReg_MEM,
  input  [2:0] DstReg_WB,
  input  [2:0] A_ID,
  input  [2:0] B_ID,
  input  MEMREAD_EX,
  output [1:0] forward_A,
  output [1:0] forward_B,
  output stall
);

  wire and_3_out, and_5_out, comparator_1_eq, comparator_2_eq, comparator_6_eq, comparator_7_eq,
       comparator_8_eq, comparator_9_eq, comparator_10_eq, comparator_11_eq, multiplexer_2_out,
       multiplexer_3_out, multiplexer_5_out, multiplexer_6_out, not_1_out, not_2_out, not_3_out, not_4_out,
       not_5_out, not_6_out, or_1_out, or_2_out, or_3_out, zeroEx, zeroMEM, zeroWB;
  wire [1:0] multiplexer_1_out, multiplexer_4_out;

  Comparator #(.width(2)) comparator_1 (.a(forward_A), .b(2'b00), .eq(comparator_1_eq));  // open: gt, lt
  not not_1 (not_1_out, comparator_1_eq);
  not not_2 (not_2_out, comparator_2_eq);
  Comparator #(.width(2)) comparator_2 (.a(forward_B), .b(2'b00), .eq(comparator_2_eq));  // open: gt, lt
  Comparator #(.width(3)) comparator_3 (.a(DstReg_Ex), .b(3'b000), .eq(zeroEx));  // open: gt, lt
  Comparator #(.width(3)) comparator_4 (.a(DstReg_MEM), .b(3'b000), .eq(zeroMEM));  // open: gt, lt
  Comparator #(.width(3)) comparator_5 (.a(DstReg_WB), .b(3'b000), .eq(zeroWB));  // open: gt, lt
  or or_1 (or_1_out, not_1_out, not_2_out);
  Comparator #(.width(3)) comparator_6 (.a(DstReg_Ex), .b(A_ID), .eq(comparator_6_eq));  // open: gt, lt
  Comparator #(.width(3)) comparator_7 (.a(DstReg_MEM), .b(A_ID), .eq(comparator_7_eq));  // open: gt, lt
  Comparator #(.width(3)) comparator_8 (.a(DstReg_WB), .b(A_ID), .eq(comparator_8_eq));  // open: gt, lt
  and and_1 (stall, or_1_out, MEMREAD_EX);
  Multiplexer multiplexer_1 (.in0(comparator_6_eq), .in1(1'b0), .out(multiplexer_1_out[0]), .sel(zeroEx));  // open: en
  Multiplexer multiplexer_2 (.in0(comparator_7_eq), .in1(1'b0), .out(multiplexer_2_out), .sel(zeroMEM));  // open: en
  Multiplexer multiplexer_3 (.in0(comparator_8_eq), .in1(1'b0), .out(multiplexer_3_out), .sel(zeroWB));  // open: en
  Comparator #(.width(3)) comparator_9 (.a(DstReg_Ex), .b(B_ID), .eq(comparator_9_eq));  // open: gt, lt
  Comparator #(.width(3)) comparator_10 (.a(DstReg_MEM), .b(B_ID), .eq(comparator_10_eq));  // open: gt, lt
  Comparator #(.width(3)) comparator_11 (.a(DstReg_WB), .b(B_ID), .eq(comparator_11_eq));  // open: gt, lt
  Multiplexer multiplexer_4 (.in0(comparator_9_eq), .in1(1'b0), .out(multiplexer_4_out[0]), .sel(zeroEx));  // open: en
  Multiplexer multiplexer_5 (.in0(comparator_10_eq), .in1(1'b0), .out(multiplexer_5_out), .sel(zeroMEM));  // open: en
  Multiplexer multiplexer_6 (.in0(comparator_11_eq), .in1(1'b0), .out(multiplexer_6_out), .sel(zeroWB));  // open: en
  not not_3 (not_3_out, multiplexer_1_out[0]);
  and and_2 (multiplexer_1_out[1], not_3_out, multiplexer_2_out);
  or or_2 (or_2_out, multiplexer_1_out[0], multiplexer_1_out[1]);
  not not_4 (not_4_out, multiplexer_4_out[0]);
  not not_5 (not_5_out, or_2_out);
  and and_3 (and_3_out, not_5_out, multiplexer_3_out);
  and and_4 (multiplexer_4_out[1], not_4_out, multiplexer_5_out);
  not not_6 (not_6_out, or_3_out);
  or or_3 (or_3_out, multiplexer_4_out[0], multiplexer_4_out[1]);
  Multiplexer #(.width(2)) multiplexer_7 (
    .in0(multiplexer_1_out), .in1(2'b11), .out(forward_A), .sel(and_3_out));  // open: en
  Multiplexer #(.width(2)) multiplexer_8 (
    .in0(multiplexer_4_out), .in1(2'b11), .out(forward_B), .sel(and_5_out));  // open: en
  and and_5 (and_5_out, not_6_out, multiplexer_6_out);
endmodule
