// Logisim project ALU_16bit .circ as structural Verilog: 1 circuit, main circuit ALU
module ALU (
  input  [15:0] A,
  input  [1:0] op_type,
  input  [15:0] B,
  input  [1:0] OP,
  output lessThan,
  output greaterThan,
  output overFlow,
  output zeroFlag,
  output carryOut,
  output [15:0] Result
);

  wire [15:0] n16_bit_arith_1_result, n16bit_logicunit_1_out_4, n16bit_shiftunit_1_out_4;

  _16_bit_Arith u_16_bit_arith_1 (
    .A(A), .B(B), .SUB(OP[0]), .RESULT(n16_bit_arith_1_result), .CARRYOUT(carryOut), .ZeroFlag(zeroFlag),
    .OverFlow(overFlow), .LessThan(lessThan), .GreaterThan(greaterThan));
  _16bit_LogicUnit u_16bit_logicunit_1 (.A(A), .B(B), .out_4(n16bit_logicunit_1_out_4), .OP(OP));
  _16bit_ShiftUnit u_16bit_shiftunit_1 (.A(A), .out_4(n16bit_shiftunit_1_out_4), .OP(OP), .B(B));
  Multiplexer #(.select(2), .width(16)) multiplexer_1 (
    .in0(n16_bit_arith_1_result), .in1(n16bit_logicunit_1_out_4), .in2(n16bit_shiftunit_1_out_4),
    .out(Result), .sel(op_type));  // open: in3, en
endmodule
