// Logisim project Branch_contUnit.circ as structural Verilog: 1 circuit, main circuit Branch_control_unit
// Branch_contUnit
module Branch_control_unit (
  input  [3:0] opCode,
  input  [2:0] RT,
  input  ZeroFlag,
  input  LessThan,
  input  GreaterThan,
  output Branch
);

  wire and_1_out, and_2_out, and_3_out, and_4_out, and_5_out, and_6_out, and_7_out, and_8_out, BEQ, BGT,
       BGTZ_BGEZ, BLT, BLTZ_BLEZ, BNE, multiplexer_1_out, multiplexer_2_out, not_1_out, or_1_out, or_2_out;

  Decoder #(.select(4)) decoder_1 (
    .out4(BEQ), .out5(BNE), .out12(BLTZ_BLEZ), .out13(BLT), .out14(BGTZ_BGEZ), .out15(BGT), .sel(opCode));  // open: out0, out1, out2, out3, out6, out7, out8, out9, out10, out11, en
  not not_1 (not_1_out, ZeroFlag);
  or or_1 (or_1_out, ZeroFlag, LessThan);
  or or_2 (or_2_out, ZeroFlag, GreaterThan);
  and and_1 (and_1_out, BEQ, ZeroFlag);
  and and_2 (and_2_out, BNE, not_1_out);
  and and_3 (and_3_out, BLT, LessThan);
  and and_4 (and_4_out, BGT, GreaterThan);
  and and_5 (and_5_out, BLTZ_BLEZ, LessThan);
  and and_6 (and_6_out, BLTZ_BLEZ, or_1_out);
  and and_7 (and_7_out, BGTZ_BGEZ, GreaterThan);
  and and_8 (and_8_out, BGTZ_BGEZ, or_2_out);
  Multiplexer multiplexer_1 (.in0(and_5_out), .in1(and_6_out), .out(multiplexer_1_out), .sel(RT[0]));  // open: en
  Multiplexer multiplexer_2 (.in0(and_7_out), .in1(and_8_out), .out(multiplexer_2_out), .sel(RT[0]));  // open: en
  or or_3 (Branch, and_1_out, and_2_out, and_3_out, and_4_out, multiplexer_1_out, multiplexer_2_out);

  // Other names for the same wires on the sheet: RT_t = RT[0]
endmodule
