// Logisim project CPU.circ as structural Verilog: 3 circuits, main circuit main
module main (
);

  wire AluSrc, and_1_out, and_4_out, BRANCH, BZ, CarryOut, CLK, constReg, Equal, ExtendOp, greaterThan, J,
       JALR, JR, lessThan, LUI, MemRd, MemToReg, MemWr, not_1_out, overFlow, RegDst, RegWr, SetLess, TrueB,
       Unsigned, ZeroFlag;
  wire [1:0] ALU_OP, Op_type;
  wire [2:0] constRegV, FUNCTION, multiplexer_3_out, multiplexer_4_out;
  wire [3:0] last4;
  wire [11:0] PC;
  wire [15:0] A, B, Br_PC, ImmEX16, J_PC, LessThanResult, LUIMM, memOutput, multiplexer_1_out,
       multiplexer_2_out, multiplexer_7_out, PC_1, Result, WD1, WD2, WD3, WD4, WrData;
  wire [15:3] Instruction;

  Clock u_CLK (.out(CLK));
  Adder #(.width(16)) adder_1 (.a({last4, PC}), .b(16'h1), .out(PC_1));  // open: cin, cout
  Multiplexer #(.width(16)) multiplexer_1 (.in0(PC_1), .in1(Br_PC), .out(multiplexer_1_out), .sel(TrueB));  // open: en
  Multiplexer #(.width(16)) multiplexer_2 (
    .in0(multiplexer_1_out), .in1(J_PC), .out(multiplexer_2_out), .sel(J));  // open: en
  PC_main main_1 (.newPc(multiplexer_2_out), .PC({last4, PC}), .CLK(CLK));  // open: Reset
  comp_contUnit comp_contunit_1 (
    .Unsigned(Unsigned), .Equal(Equal), .Lessthan(lessThan), .zeroFlag(ZeroFlag), .carryOut(CarryOut),
    .LessThanResult(LessThanResult));
  Branch_control_unit branch_control_unit_1 (
    .opCode(Instruction[15:12]), .RT(Instruction[8:6]), .ZeroFlag(ZeroFlag), .LessThan(lessThan),
    .GreaterThan(greaterThan), .Branch(TrueB));
  ROM #(.addrWidth(12), .dataWidth(16)) rom_1 (.addr(PC), .data({Instruction, FUNCTION}));  // open: sel
  Multiplexer #(.width(3)) multiplexer_3 (
    .in0(Instruction[8:6]), .in1(Instruction[5:3]), .out(multiplexer_3_out), .sel(RegDst));  // open: en
  Multiplexer #(.width(3)) multiplexer_4 (
    .in0(multiplexer_3_out), .in1(constRegV), .out(multiplexer_4_out), .sel(constReg));  // open: en
  Shifter #(.width(16)) shifter_1 (.in({Instruction, FUNCTION}), .\dist (4'b1000), .out(LUIMM));
  RegisterFile registerfile_1 (
    .Read_Register_1(Instruction[11:9]), .Read_Register_2(Instruction[8:6]),
    .Write_Register(multiplexer_4_out), .Write_Data(WrData), .Data_1(A), .Data_2(B), .regWrite(RegWr),
    .Clock(CLK));
  assign ImmEX16 = {{10{Instruction[5]}}, {Instruction[5:3], FUNCTION}};  // Bit_Extender bit_extender_1
  Adder #(.width(16)) adder_2 (.a({last4, PC}), .b(ImmEX16), .out(Br_PC), .cin(1'b1));  // open: cout
  Multiplexer #(.width(16)) multiplexer_5 (
    .in0({last4, Instruction[11:3], FUNCTION}), .in1(A), .out(J_PC), .sel(JR));  // open: en
  Control_unit control_unit_1 (
    .OPcode(Instruction[15:12]), .Function(FUNCTION), .RegDst(RegDst), .RegWr(RegWr), .ExtendOp(ExtendOp),
    .AluSrc(AluSrc), .MemRd(MemRd), .MemWr(MemWr), .MemToReg(MemToReg), .BRANCH(BRANCH), .JUMP(J),
    .SeltLess(SetLess), .Equal(Equal), .Unsigned(Unsigned), .ALU_OP(ALU_OP), .OP_TYPE(Op_type), .BZ(BZ),
    .LUI(LUI), .CONSTREG(constReg));
  and and_1 (and_1_out, LUI, constReg);
  Multiplexer #(.width(3)) multiplexer_6 (.in0(3'b111), .in1(3'b001), .out(constRegV), .sel(and_1_out));  // open: en
  Multiplexer #(.width(16)) multiplexer_7 (.in0(B), .in1(ImmEX16), .out(multiplexer_7_out), .sel(AluSrc));  // open: en
  Multiplexer #(.width(16)) multiplexer_8 (.in0(WD4), .in1(LessThanResult), .out(WrData), .sel(SetLess));  // open: en
  ALU alu_1 (
    .A(A), .B(multiplexer_7_out), .lessThan(lessThan), .greaterThan(greaterThan), .overFlow(overFlow),
    .zeroFlag(ZeroFlag), .carryOut(CarryOut), .Result(Result), .OP(ALU_OP), .op_type(Op_type));
  Multiplexer #(.width(16)) multiplexer_9 (.in0(WD1), .in1(WD2), .out(WD3), .sel(constReg));  // open: en
  Multiplexer #(.width(16)) multiplexer_10 (.in0(WD3), .in1(PC_1), .out(WD4), .sel(JALR));  // open: en
  Multiplexer #(.width(16)) multiplexer_11 (.in0(Result), .in1(memOutput), .out(WD1), .sel(MemToReg));  // open: en
  Multiplexer #(.width(16)) multiplexer_12 (.in0(PC_1), .in1(LUIMM), .out(WD2), .sel(and_4_out));  // open: en
  and and_2 (JR, RegDst, not_1_out, J);
  and and_3 (JALR, RegDst, RegWr, J);
  and and_4 (and_4_out, LUI, constReg);
  not not_1 (not_1_out, RegWr);
  RAM #(.addrWidth(12), .dataWidth(16), .bus("separate")) ram_1 (
    .addr(Result[11:0]), .din(B), .data(memOutput), .str(MemWr), .clk(CLK), .ld(MemRd));  // open: sel, clr

  // Other names for the same wires on the sheet: Instruction[2:0] = FUNCTION; Rd[2:0] = Instruction[5:3];
  //   Rt[2:0] = Instruction[8:6]; Rs[2:0] = Instruction[11:9]; PC[15:12] = last4; OP_code[3:0] = Instruction[15:12]

  // Notes on the sheet:
  //   PC
  //   LESS THAN CONTROLER
  //   BRANCH CONTROLER
  //   INSTRCION MEMORY
  //   contents of rom_1 (hex, n*v repeats v):
  //   a384 8354 35b 2040 2081 20c2 890a 1921 1520 14f2 4c02 1290 403b 3100 b011 55c 1b68 4e9 2040 2285
  //   22c6 4e0 3100 1e06
  //   INSTRUCTION DECODER
  //   REGISTER FILE
  //   CONTROL UNIT
  //   ALU
  //   Write Data Controler
  //   DATA MEMORY
endmodule

module RegisterFile (
  input  regWrite,
  input  [15:0] Write_Data,
  input  Clock,
  input  [2:0] Read_Register_1,
  input  [2:0] Read_Register_2,
  input  [2:0] Write_Register,
  output [15:0] Data_1,
  output [15:0] Data_2
);

  wire and_1_out, and_2_out, and_3_out, and_4_out, and_5_out, and_6_out, and_7_out, and_8_out,
       decoder_1_out0, decoder_1_out1, decoder_1_out2, decoder_1_out3, decoder_1_out4, decoder_1_out5,
       decoder_1_out6, decoder_1_out7;
  wire [15:0] register_1_q, register_2_q, register_3_q, register_4_q, register_5_q, register_6_q,
       register_7_q, register_8_q;

  Decoder #(.select(3)) decoder_1 (
    .out0(decoder_1_out0), .out1(decoder_1_out1), .out2(decoder_1_out2), .out3(decoder_1_out3),
    .out4(decoder_1_out4), .out5(decoder_1_out5), .out6(decoder_1_out6), .out7(decoder_1_out7),
    .sel(Write_Register));  // open: en
  and and_1 (and_1_out, decoder_1_out0, 1'b0, regWrite);
  and and_2 (and_2_out, decoder_1_out1, regWrite);
  and and_3 (and_3_out, decoder_1_out2, regWrite);
  and and_4 (and_4_out, decoder_1_out3, regWrite);
  and and_5 (and_5_out, decoder_1_out4, regWrite);
  and and_6 (and_6_out, decoder_1_out5, regWrite);
  and and_7 (and_7_out, decoder_1_out6, regWrite);
  and and_8 (and_8_out, decoder_1_out7, regWrite);
  Register #(.width(16)) register_1 (.D(Write_Data), .en(and_1_out), .Q(register_1_q), .clk(Clock));  // open: clr
  Register #(.width(16)) register_2 (.D(Write_Data), .en(and_2_out), .Q(register_2_q), .clk(Clock));  // open: clr
  Register #(.width(16)) register_3 (.D(Write_Data), .en(and_3_out), .Q(register_3_q), .clk(Clock));  // open: clr
  Register #(.width(16)) register_4 (.D(Write_Data), .en(and_4_out), .Q(register_4_q), .clk(Clock));  // open: clr
  Register #(.width(16)) register_5 (.D(Write_Data), .en(and_5_out), .Q(register_5_q), .clk(Clock));  // open: clr
  Register #(.width(16)) register_6 (.D(Write_Data), .en(and_6_out), .Q(register_6_q), .clk(Clock));  // open: clr
  Register #(.width(16)) register_7 (.D(Write_Data), .en(and_7_out), .Q(register_7_q), .clk(Clock));  // open: clr
  Register #(.width(16)) register_8 (.D(Write_Data), .en(and_8_out), .Q(register_8_q), .clk(Clock));  // open: clr
  Multiplexer #(.select(3), .width(16)) multiplexer_1 (
    .in0(register_1_q), .in1(register_2_q), .in2(register_3_q), .in3(register_4_q), .in4(register_5_q),
    .in5(register_6_q), .in6(register_7_q), .in7(register_8_q), .out(Data_2), .sel(Read_Register_2));  // open: en
  Multiplexer #(.select(3), .width(16)) multiplexer_2 (
    .in0(register_1_q), .in1(register_2_q), .in2(register_3_q), .in3(register_4_q), .in4(register_5_q),
    .in5(register_6_q), .in6(register_7_q), .in7(register_8_q), .out(Data_1), .sel(Read_Register_1));  // open: en
endmodule

// LessThan_contUnit
module comp_contUnit (
  input  Unsigned,
  input  Equal,
  input  Lessthan,
  input  zeroFlag,
  input  carryOut,
  output [15:0] LessThanResult
);

  wire multiplexer_1_out, multiplexer_2_out, multiplexer_3_out, not_1_out, not_2_out, or_1_out, or_2_out;

  not not_1 (not_1_out, carryOut);
  or or_1 (or_1_out, Lessthan, zeroFlag);
  not not_2 (not_2_out, carryOut);
  or or_2 (or_2_out, not_1_out, zeroFlag);
  Multiplexer multiplexer_1 (.in0(Lessthan), .in1(or_1_out), .out(multiplexer_1_out), .sel(Equal));  // open: en
  Multiplexer multiplexer_2 (.in0(not_2_out), .in1(or_2_out), .out(multiplexer_2_out), .sel(Equal));  // open: en
  Multiplexer multiplexer_3 (
    .in0(multiplexer_1_out), .in1(multiplexer_2_out), .out(multiplexer_3_out), .sel(Unsigned));  // open: en
  assign LessThanResult = {{15{1'b0}}, multiplexer_3_out};  // Bit_Extender bit_extender_1
endmodule
