// Logisim project PC.circ as structural Verilog: 1 circuit, main circuit main
module main (
  input  [15:0] newPc,
  input  CLK,
  input  Reset,
  output [15:0] PC
);

  Register #(.width(16)) register_1 (.D(newPc), .Q(PC), .clk(CLK), .clr(Reset));  // open: en
endmodule
