// Logisim project Register File.circ as structural Verilog: 2 circuits, main circuit main
module main (
  input  [2:0] Read_Register_1,
  input  [2:0] Read_Register_2,
  input  [2:0] Write_Register,
  input  [15:0] Write_Data,
  input  regWrite,
  input  CLK,
  output [15:0] Data_1,
  output [15:0] Data_2
);

  _16_Bit_Register u_16_bit_register_1 (
    .Read_Register_1(Read_Register_1), .Read_Register_2(Read_Register_2), .Write_Register(Write_Register),
    .Write_Data(Write_Data), .regWrite(regWrite), .Clock(CLK), .Data_1(Data_1), .Data_2(Data_2));
endmodule

module _16_Bit_Register (
  input  [2:0] Read_Register_1,
  input  [2:0] Read_Register_2,
  input  [2:0] Write_Register,
  input  regWrite,
  input  Clock,
  input  [15:0] Write_Data,
  output [15:0] Data_1,
  output [15:0] Data_2
);

  wire and_1_out, and_2_out, and_3_out, and_4_out, and_5_out, and_6_out, and_7_out, and_8_out,
       decoder_1_out0, decoder_1_out1, decoder_1_out2, decoder_1_out3, decoder_1_out4, decoder_1_out5,
       decoder_1_out6, decoder_1_out7;
  wire [15:0] register_1_q, register_2_q, register_3_q, register_4_q, register_5_q, register_6_q,
       register_7_q, register_8_q;

  Decoder #(.select(3)) decoder_1 (
    .out0(decoder_1_out0), .out1(decoder_1_out1), .out2(decoder_1_out2), .out3(decoder_1_out3),
    .out4(decoder_1_out4), .out5(decoder_1_out5), .out6(decoder_1_out6), .out7(decoder_1_out7),
    .sel(Write_Register));  // open: en
  and and_1 (and_1_out, decoder_1_out0, 1'b0, regWrite);
  and and_2 (and_2_out, decoder_1_out1, regWrite);
  and and_3 (and_3_out, decoder_1_out2, regWrite);
  and and_4 (and_4_out, decoder_1_out3, regWrite);
  and and_5 (and_5_out, decoder_1_out4, regWrite);
  and and_6 (and_6_out, decoder_1_out5, regWrite);
  and and_7 (and_7_out, decoder_1_out6, regWrite);
  and and_8 (and_8_out, decoder_1_out7, regWrite);
  Register #(.width(16)) register_1 (.D(Write_Data), .en(and_1_out), .Q(register_1_q), .clk(Clock));  // open: clr
  Register #(.width(16)) register_2 (.D(Write_Data), .en(and_2_out), .Q(register_2_q), .clk(Clock));  // open: clr
  Register #(.width(16)) register_3 (.D(Write_Data), .en(and_3_out), .Q(register_3_q), .clk(Clock));  // open: clr
  Register #(.width(16)) register_4 (.D(Write_Data), .en(and_4_out), .Q(register_4_q), .clk(Clock));  // open: clr
  Register #(.width(16)) register_5 (.D(Write_Data), .en(and_5_out), .Q(register_5_q), .clk(Clock));  // open: clr
  Register #(.width(16)) register_6 (.D(Write_Data), .en(and_6_out), .Q(register_6_q), .clk(Clock));  // open: clr
  Register #(.width(16)) register_7 (.D(Write_Data), .en(and_7_out), .Q(register_7_q), .clk(Clock));  // open: clr
  Register #(.width(16)) register_8 (.D(Write_Data), .en(and_8_out), .Q(register_8_q), .clk(Clock));  // open: clr
  Multiplexer #(.select(3), .width(16)) multiplexer_1 (
    .in0(register_1_q), .in1(register_2_q), .in2(register_3_q), .in3(register_4_q), .in4(register_5_q),
    .in5(register_6_q), .in6(register_7_q), .in7(register_8_q), .out(Data_2), .sel(Read_Register_2));  // open: en
  Multiplexer #(.select(3), .width(16)) multiplexer_2 (
    .in0(register_1_q), .in1(register_2_q), .in2(register_3_q), .in3(register_4_q), .in4(register_5_q),
    .in5(register_6_q), .in6(register_7_q), .in7(register_8_q), .out(Data_1), .sel(Read_Register_1));  // open: en
endmodule
